# Fritzing sketch Bargraph (Advanced) (saved by Fritzing 0.7.0b)
breadboards: 1

parts:
  Arduino1 = Arduino
  LED1 = LED - 5mm [color="Red (633nm)" package="5 mm [THT]"]
  LED2 = LED - 5mm [color="Red (633nm)" package="5 mm [THT]"]
  LED3 = LED - 5mm [color="Yellow (585nm)" package="5 mm [THT]"]
  LED4 = LED - 5mm [color="Yellow (585nm)" package="5 mm [THT]"]
  LED5 = LED - 5mm [color="Green (555nm)" package="5 mm [THT]"]
  LED6 = LED - 5mm [color="Green (555nm)" package="5 mm [THT]"]

nets:
  N1: Arduino1.GND, LED1.anode, LED2.anode, LED3.anode, LED4.anode, LED5.anode, LED6.anode
  N2: Arduino1.D11, LED1.cathode
  N3: Arduino1.D10, LED2.cathode
  N4: Arduino1.D9, LED3.cathode
  N5: Arduino1.D6, LED4.cathode
  N6: Arduino1.D5, LED6.cathode
  N7: Arduino1.D2, LED5.cathode
