# Fritzing sketch Bargraph (Analog) (saved by Fritzing 0.9.2b)
breadboards: 1

parts:
  LED7 = LED - 5mm [color="Red (635nm)" package="5 mm [THT]"]
  LED8 = LED - 5mm [color="Red (635nm)" package="5 mm [THT]"]
  LED9 = LED - 5mm [color="Yellow (585nm)" package="5 mm [THT]"]
  LED10 = LED - 5mm [color="Yellow (585nm)" package="5 mm [THT]"]
  LED11 = LED - 5mm [color="Green (560nm)" package="5 mm [THT]"]
  LED12 = LED - 5mm [color="Green (560nm)" package="5 mm [THT]"]
  R7 = Resistor [tolerance=±5% resistance=220 package=THT]
  R8 = Resistor [tolerance=±5% resistance=220 package=THT]
  R9 = Resistor [tolerance=±5% resistance=220 package=THT]
  R10 = Resistor [tolerance=±5% resistance=220 package=THT]
  R11 = Resistor [tolerance=±5% resistance=220 package=THT]
  R12 = Resistor [tolerance=±5% resistance=220 package=THT]
  Arduino2 = Arduino Uno (Rev3)

nets:
  N1: LED7.anode, R8.Pin_0
  N2: LED8.anode, R7.Pin_0
  N3: LED9.anode, R9.Pin_0
  N4: LED10.anode, R10.Pin_0
  N5: LED11.anode, R11.Pin_0
  N6: LED12.anode, R12.Pin_0
  N7: R7.Pin_1, R8.Pin_1, R9.Pin_1, R10.Pin_1, R11.Pin_1, R12.Pin_1, Arduino2.GND
