# Fritzing sketch Physical Pixel (saved by Fritzing 0.9.2b)
circuit board: 6.88566cm x 5.36311cm
breadboards: 1

parts:
  LED1 = RGB LED - (4 legs) [package="5 mm [THT]"]
  R1 = Resistor [tolerance=±5% resistance=220 package=THT]
  R2 = Resistor [tolerance=±5% resistance=220 package=THT]
  R3 = Resistor [tolerance=±5% resistance=220 package=THT]
  part = RGB LED - (4 legs) [package="5 mm [THT]"]  # not connected
  RGB_Shield = Arduino Uno (Rev3)

nets:
  N1: LED1.red_cathode, R1.Pin_0
  N2: LED1.common_anode, RGB_Shield.GND
  N3: LED1.green_cathode, R2.Pin_0
  N4: LED1.blue_cathode, R3.Pin_0
