# Fritzing sketch Capacitive Sensing (saved by Fritzing 0.9.2b)
breadboards: 1

parts:
  R1 = Resistor [tolerance=±5% resistance=1M package=THT]
  RGB_Shield = Arduino Uno (Rev3)

nets:
  N1: R1.Pin_1, RGB_Shield.D2
